// Logisim project ALU_Group29_v2.circ as structural Verilog: 6 circuits, main circuit main
module main (
  output halt,
  output [15:0] counter,
  output [3:0] op,
  output [15:0] a,
  output [15:0] b,
  output [15:0] oracle,
  output [15:0] result,
  output err_oracle,
  output error,
  output ok
);

  wire and_1_out, and_2_out, clock_1_out, comparator_1_eq, comparator_2_eq;

  Clock clock_1 (.out(clock_1_out));
  Counter #(.width(16), .max('hffff), .trigger("falling")) counter_1 (
    .Q(counter), .carry(halt), .clk(clock_1_out));  // open: load, D, count, clr
  RAM #(.addrWidth(19), .dataWidth(4), .bus("separate")) ram_1 (
    .addr({counter, 3'b000}), .data(op), .ld(1'b1));  // open: din, str, sel, clk, clr
  RAM #(.addrWidth(19), .dataWidth(16), .bus("separate")) ram_2 (
    .addr({counter, 3'b001}), .data(a), .ld(1'b1));  // open: din, str, sel, clk, clr
  RAM #(.addrWidth(19), .dataWidth(16), .bus("separate")) ram_3 (
    .addr({counter, 3'b010}), .data(b), .ld(1'b1));  // open: din, str, sel, clk, clr
  RAM #(.addrWidth(19), .dataWidth(16), .bus("separate")) ram_4 (
    .addr({counter, 3'b011}), .data(oracle), .ld(1'b1));  // open: din, str, sel, clk, clr
  RAM #(.addrWidth(19), .dataWidth(1), .bus("separate")) ram_5 (
    .addr({counter, 3'b100}), .data(err_oracle), .ld(1'b1));  // open: din, str, sel, clk, clr
  _16_bit_ALU u_16_bit_alu_1 (.opcode(op), .a(a), .b(b), .overflow(error), .result(result));  // open: zero
  Comparator #(.width(1), .mode("unsigned")) comparator_1 (
    .a(error), .b(err_oracle), .eq(comparator_1_eq));  // open: gt, lt
  Comparator #(.width(16)) comparator_2 (.a(result), .b(oracle), .eq(comparator_2_eq));  // open: gt, lt
  and and_1 (and_1_out, comparator_1_eq, error);
  and and_2 (and_2_out, comparator_2_eq, comparator_1_eq, ~error);  // AND_Gate
  or or_1 (ok, and_1_out, and_2_out);

  // Notes on the sheet:
  //   You must complete the circuit '16-bit ALU' instead.
  //   DO NOT EDIT THIS CIRCUIT!
  //   operation
  //   operand a
  //   operand b
  //   expected result
  //   expected error value
endmodule

// ALU
module _16_bit_ALU (
  input  [3:0] opcode,
  input  [15:0] a,
  input  [15:0] b,
  output overflow,
  output zero,
  output [15:0] result
);

  wire n1_bit_alu_1_carryout, n1_bit_alu_1_carryout_great, n1_bit_alu_1_carryout_inv,
       n1_bit_alu_1_carryout_less, n1_bit_alu_2_carryout, n1_bit_alu_2_carryout_great,
       n1_bit_alu_2_carryout_inv, n1_bit_alu_2_carryout_less, n1_bit_alu_3_carryout,
       n1_bit_alu_3_carryout_great, n1_bit_alu_3_carryout_inv, n1_bit_alu_3_carryout_less,
       n1_bit_alu_4_carryout, n1_bit_alu_4_carryout_great, n1_bit_alu_4_carryout_inv,
       n1_bit_alu_4_carryout_less, n1_bit_alu_5_carryout, n1_bit_alu_5_carryout_great,
       n1_bit_alu_5_carryout_inv, n1_bit_alu_5_carryout_less, n1_bit_alu_6_carryout,
       n1_bit_alu_6_carryout_great, n1_bit_alu_6_carryout_inv, n1_bit_alu_6_carryout_less,
       n1_bit_alu_7_carryout, n1_bit_alu_7_carryout_great, n1_bit_alu_7_carryout_inv,
       n1_bit_alu_7_carryout_less, n1_bit_alu_8_carryout, n1_bit_alu_8_carryout_great,
       n1_bit_alu_8_carryout_inv, n1_bit_alu_8_carryout_less, n1_bit_alu_9_carryout,
       n1_bit_alu_9_carryout_great, n1_bit_alu_9_carryout_inv, n1_bit_alu_9_carryout_less,
       n1_bit_alu_10_carryout, n1_bit_alu_10_carryout_great, n1_bit_alu_10_carryout_inv,
       n1_bit_alu_10_carryout_less, n1_bit_alu_11_carryout, n1_bit_alu_11_carryout_great,
       n1_bit_alu_11_carryout_inv, n1_bit_alu_11_carryout_less, n1_bit_alu_12_carryout,
       n1_bit_alu_12_carryout_great, n1_bit_alu_12_carryout_inv, n1_bit_alu_12_carryout_less,
       n1_bit_alu_13_carryout, n1_bit_alu_13_carryout_great, n1_bit_alu_13_carryout_inv,
       n1_bit_alu_13_carryout_less, n1_bit_alu_14_carryout, n1_bit_alu_14_carryout_great,
       n1_bit_alu_14_carryout_inv, n1_bit_alu_14_carryout_less, n1_bit_alu_lsb_1_carryout,
       n1_bit_alu_lsb_1_carryout_great, n1_bit_alu_lsb_1_carryout_inv, n1_bit_alu_lsb_1_carryout_less,
       n1_bit_alu_msb_1_set_less;
  wire [15:0] n1_bit_alu_lsb_1_result;

  _1_bit_ALU_LSB u_1_bit_alu_lsb_1 (
    .A(a[0]), .B(b[0]), .less(n1_bit_alu_msb_1_set_less), .carryOut_less(n1_bit_alu_lsb_1_carryout_less),
    .carryOut(n1_bit_alu_lsb_1_carryout), .carryOut_inv(n1_bit_alu_lsb_1_carryout_inv), .selector(opcode),
    .result(n1_bit_alu_lsb_1_result[0]), .carryOut_Great(n1_bit_alu_lsb_1_carryout_great));
  _1_bit_ALU u_1_bit_alu_1 (
    .A(a[1]), .B(b[1]), .carryIn_less(n1_bit_alu_lsb_1_carryout_less), .carryIn(n1_bit_alu_lsb_1_carryout),
    .carryIn_inv(n1_bit_alu_lsb_1_carryout_inv), .carryIn_Great(n1_bit_alu_lsb_1_carryout_great),
    .carryOut_less(n1_bit_alu_1_carryout_less), .carryOut(n1_bit_alu_1_carryout),
    .carryOut_inv(n1_bit_alu_1_carryout_inv), .selector(opcode), .result(n1_bit_alu_lsb_1_result[1]),
    .carryOut_Great(n1_bit_alu_1_carryout_great));
  _1_bit_ALU u_1_bit_alu_2 (
    .A(a[2]), .B(b[2]), .carryIn_less(n1_bit_alu_1_carryout_less), .carryIn(n1_bit_alu_1_carryout),
    .carryIn_inv(n1_bit_alu_1_carryout_inv), .carryIn_Great(n1_bit_alu_1_carryout_great),
    .carryOut_less(n1_bit_alu_2_carryout_less), .carryOut(n1_bit_alu_2_carryout),
    .carryOut_inv(n1_bit_alu_2_carryout_inv), .selector(opcode), .result(n1_bit_alu_lsb_1_result[2]),
    .carryOut_Great(n1_bit_alu_2_carryout_great));
  _1_bit_ALU u_1_bit_alu_3 (
    .A(a[3]), .B(b[3]), .carryIn_less(n1_bit_alu_2_carryout_less), .carryIn(n1_bit_alu_2_carryout),
    .carryIn_inv(n1_bit_alu_2_carryout_inv), .carryIn_Great(n1_bit_alu_2_carryout_great),
    .carryOut_less(n1_bit_alu_3_carryout_less), .carryOut(n1_bit_alu_3_carryout),
    .carryOut_inv(n1_bit_alu_3_carryout_inv), .selector(opcode), .result(n1_bit_alu_lsb_1_result[3]),
    .carryOut_Great(n1_bit_alu_3_carryout_great));
  _1_bit_ALU u_1_bit_alu_4 (
    .A(a[4]), .B(b[4]), .carryIn_less(n1_bit_alu_3_carryout_less), .carryIn(n1_bit_alu_3_carryout),
    .carryIn_inv(n1_bit_alu_3_carryout_inv), .carryIn_Great(n1_bit_alu_3_carryout_great),
    .carryOut_less(n1_bit_alu_4_carryout_less), .carryOut(n1_bit_alu_4_carryout),
    .carryOut_inv(n1_bit_alu_4_carryout_inv), .selector(opcode), .result(n1_bit_alu_lsb_1_result[4]),
    .carryOut_Great(n1_bit_alu_4_carryout_great));
  _1_bit_ALU u_1_bit_alu_5 (
    .A(a[5]), .B(b[5]), .carryIn_less(n1_bit_alu_4_carryout_less), .carryIn(n1_bit_alu_4_carryout),
    .carryIn_inv(n1_bit_alu_4_carryout_inv), .carryIn_Great(n1_bit_alu_4_carryout_great),
    .carryOut_less(n1_bit_alu_5_carryout_less), .carryOut(n1_bit_alu_5_carryout),
    .carryOut_inv(n1_bit_alu_5_carryout_inv), .selector(opcode), .result(n1_bit_alu_lsb_1_result[5]),
    .carryOut_Great(n1_bit_alu_5_carryout_great));
  _1_bit_ALU u_1_bit_alu_6 (
    .A(a[6]), .B(b[6]), .carryIn_less(n1_bit_alu_5_carryout_less), .carryIn(n1_bit_alu_5_carryout),
    .carryIn_inv(n1_bit_alu_5_carryout_inv), .carryIn_Great(n1_bit_alu_5_carryout_great),
    .carryOut_less(n1_bit_alu_6_carryout_less), .carryOut(n1_bit_alu_6_carryout),
    .carryOut_inv(n1_bit_alu_6_carryout_inv), .selector(opcode), .result(n1_bit_alu_lsb_1_result[6]),
    .carryOut_Great(n1_bit_alu_6_carryout_great));
  _1_bit_ALU u_1_bit_alu_7 (
    .A(a[7]), .B(b[7]), .carryIn_less(n1_bit_alu_6_carryout_less), .carryIn(n1_bit_alu_6_carryout),
    .carryIn_inv(n1_bit_alu_6_carryout_inv), .carryIn_Great(n1_bit_alu_6_carryout_great),
    .carryOut_less(n1_bit_alu_7_carryout_less), .carryOut(n1_bit_alu_7_carryout),
    .carryOut_inv(n1_bit_alu_7_carryout_inv), .selector(opcode), .result(n1_bit_alu_lsb_1_result[7]),
    .carryOut_Great(n1_bit_alu_7_carryout_great));
  _1_bit_ALU u_1_bit_alu_8 (
    .A(a[8]), .B(b[8]), .carryIn_less(n1_bit_alu_7_carryout_less), .carryIn(n1_bit_alu_7_carryout),
    .carryIn_inv(n1_bit_alu_7_carryout_inv), .carryIn_Great(n1_bit_alu_7_carryout_great),
    .carryOut_less(n1_bit_alu_8_carryout_less), .carryOut(n1_bit_alu_8_carryout),
    .carryOut_inv(n1_bit_alu_8_carryout_inv), .selector(opcode), .result(n1_bit_alu_lsb_1_result[8]),
    .carryOut_Great(n1_bit_alu_8_carryout_great));
  _1_bit_ALU u_1_bit_alu_9 (
    .A(a[9]), .B(b[9]), .carryIn_less(n1_bit_alu_8_carryout_less), .carryIn(n1_bit_alu_8_carryout),
    .carryIn_inv(n1_bit_alu_8_carryout_inv), .carryIn_Great(n1_bit_alu_8_carryout_great),
    .carryOut_less(n1_bit_alu_9_carryout_less), .carryOut(n1_bit_alu_9_carryout),
    .carryOut_inv(n1_bit_alu_9_carryout_inv), .selector(opcode), .result(n1_bit_alu_lsb_1_result[9]),
    .carryOut_Great(n1_bit_alu_9_carryout_great));
  _1_bit_ALU u_1_bit_alu_10 (
    .A(a[10]), .B(b[10]), .carryIn_less(n1_bit_alu_9_carryout_less), .carryIn(n1_bit_alu_9_carryout),
    .carryIn_inv(n1_bit_alu_9_carryout_inv), .carryIn_Great(n1_bit_alu_9_carryout_great),
    .carryOut_less(n1_bit_alu_10_carryout_less), .carryOut(n1_bit_alu_10_carryout),
    .carryOut_inv(n1_bit_alu_10_carryout_inv), .selector(opcode), .result(n1_bit_alu_lsb_1_result[10]),
    .carryOut_Great(n1_bit_alu_10_carryout_great));
  _1_bit_ALU u_1_bit_alu_11 (
    .A(a[11]), .B(b[11]), .carryIn_less(n1_bit_alu_10_carryout_less), .carryIn(n1_bit_alu_10_carryout),
    .carryIn_inv(n1_bit_alu_10_carryout_inv), .carryIn_Great(n1_bit_alu_10_carryout_great),
    .carryOut_less(n1_bit_alu_11_carryout_less), .carryOut(n1_bit_alu_11_carryout),
    .carryOut_inv(n1_bit_alu_11_carryout_inv), .selector(opcode), .result(n1_bit_alu_lsb_1_result[11]),
    .carryOut_Great(n1_bit_alu_11_carryout_great));
  _1_bit_ALU u_1_bit_alu_12 (
    .A(a[12]), .B(b[12]), .carryIn_less(n1_bit_alu_11_carryout_less), .carryIn(n1_bit_alu_11_carryout),
    .carryIn_inv(n1_bit_alu_11_carryout_inv), .carryIn_Great(n1_bit_alu_11_carryout_great),
    .carryOut_less(n1_bit_alu_12_carryout_less), .carryOut(n1_bit_alu_12_carryout),
    .carryOut_inv(n1_bit_alu_12_carryout_inv), .selector(opcode), .result(n1_bit_alu_lsb_1_result[12]),
    .carryOut_Great(n1_bit_alu_12_carryout_great));
  _1_bit_ALU u_1_bit_alu_13 (
    .A(a[13]), .B(b[13]), .carryIn_less(n1_bit_alu_12_carryout_less), .carryIn(n1_bit_alu_12_carryout),
    .carryIn_inv(n1_bit_alu_12_carryout_inv), .carryIn_Great(n1_bit_alu_12_carryout_great),
    .carryOut_less(n1_bit_alu_13_carryout_less), .carryOut(n1_bit_alu_13_carryout),
    .carryOut_inv(n1_bit_alu_13_carryout_inv), .selector(opcode), .result(n1_bit_alu_lsb_1_result[13]),
    .carryOut_Great(n1_bit_alu_13_carryout_great));
  _1_bit_ALU u_1_bit_alu_14 (
    .A(a[14]), .B(b[14]), .carryIn_less(n1_bit_alu_13_carryout_less), .carryIn(n1_bit_alu_13_carryout),
    .carryIn_inv(n1_bit_alu_13_carryout_inv), .carryIn_Great(n1_bit_alu_13_carryout_great),
    .carryOut_less(n1_bit_alu_14_carryout_less), .carryOut(n1_bit_alu_14_carryout),
    .carryOut_inv(n1_bit_alu_14_carryout_inv), .selector(opcode), .result(n1_bit_alu_lsb_1_result[14]),
    .carryOut_Great(n1_bit_alu_14_carryout_great));
  _1_bit_ALU_MSB u_1_bit_alu_msb_1 (
    .A(a[15]), .B(b[15]), .carryIn_less(n1_bit_alu_14_carryout_less), .carryIn(n1_bit_alu_14_carryout),
    .carryIn_inv(n1_bit_alu_14_carryout_inv), .carryIn_Great(n1_bit_alu_14_carryout_great),
    .set_less(n1_bit_alu_msb_1_set_less), .selector(opcode), .result(n1_bit_alu_lsb_1_result[15]),
    .overflow(overflow));
  nor nor_1 (zero, n1_bit_alu_lsb_1_result[0], n1_bit_alu_lsb_1_result[1], n1_bit_alu_lsb_1_result[2], n1_bit_alu_lsb_1_result[3], n1_bit_alu_lsb_1_result[4], n1_bit_alu_lsb_1_result[5], n1_bit_alu_lsb_1_result[6], n1_bit_alu_lsb_1_result[7], n1_bit_alu_lsb_1_result[8], n1_bit_alu_lsb_1_result[9], n1_bit_alu_lsb_1_result[10], n1_bit_alu_lsb_1_result[11], n1_bit_alu_lsb_1_result[12], n1_bit_alu_lsb_1_result[13], n1_bit_alu_lsb_1_result[14], n1_bit_alu_lsb_1_result[15]);
  Multiplexer #(.select(4), .width(16)) multiplexer_1 (
    .in0(n1_bit_alu_lsb_1_result), .in1(n1_bit_alu_lsb_1_result), .in2(n1_bit_alu_lsb_1_result),
    .in3(n1_bit_alu_lsb_1_result), .in4(n1_bit_alu_lsb_1_result), .in5(n1_bit_alu_lsb_1_result),
    .in6(n1_bit_alu_lsb_1_result), .in7(n1_bit_alu_lsb_1_result), .in8({{15{1'b0}}, zero}), .in9({16{1'b0}}),
    .in10({16{1'b0}}), .in11({16{1'b0}}), .in12({16{1'b0}}), .in13({16{1'b0}}), .in14({16{1'b0}}),
    .in15({16{1'b0}}), .out(result), .sel(opcode));  // open: en

  // Notes on the sheet:
  //   This circuit is used as a block in the main circuit, and its layout must remain unchanged.
  //   DO NOT CHANGE THE INPUTS AND OUTPUTS OF THIS CIRCUIT! Do not add/remove inputs or outputs. Do not even change their location or orientation.
endmodule

module _1_bit_ALU_LSB (
  input  A,
  input  B,
  input  less,
  input  [3:0] selector,
  output result,
  output carryOut_Great,
  output carryOut_less,
  output carryOut,
  output carryOut_inv
);

  wire and_1_out, n1_bit_adder_1_sum, n1_bit_adder_2_sum, n1_bit_adder_4_sum, not_1_out, not_2_out,
       not_3_out, not_4_out, not_5_out, or_1_out;

  _1_bit_adder u_1_bit_adder_1 (.a(A), .b(B), .carryIn(1'b0), .carryOut(carryOut), .sum(n1_bit_adder_1_sum));
  not not_1 (not_1_out, B);
  not not_2 (not_2_out, B);
  and and_1 (and_1_out, A, B);
  or or_1 (or_1_out, A, B);
  not not_3 (not_3_out, A);
  not not_4 (not_4_out, A);
  _1_bit_adder u_1_bit_adder_2 (
    .a(not_4_out), .b(1'b0), .carryIn(1'b1), .carryOut(carryOut_inv), .sum(n1_bit_adder_2_sum));
  _1_bit_adder u_1_bit_adder_3 (.a(A), .b(not_1_out), .carryIn(1'b1), .carryOut(carryOut_less));  // open: sum
  _1_bit_adder u_1_bit_adder_4 (.a(A), .b(not_2_out), .carryIn(1'b1), .sum(n1_bit_adder_4_sum));  // open: carryOut
  not not_5 (not_5_out, A);
  _1_bit_adder u_1_bit_adder_5 (.a(not_5_out), .b(B), .carryIn(1'b1), .carryOut(carryOut_Great));  // open: sum
  Multiplexer #(.select(4)) multiplexer_1 (
    .in0(1'b0), .in1(and_1_out), .in2(or_1_out), .in3(not_3_out), .in4(n1_bit_adder_1_sum),
    .in5(n1_bit_adder_2_sum), .in6(less), .in7(less), .in8(n1_bit_adder_4_sum), .out(result), .sel(selector));  // open: in9, in10, in11, in12, in13, in14, in15, en
endmodule

module _1_bit_ALU (
  input  carryIn_less,
  input  carryIn,
  input  carryIn_inv,
  input  carryIn_Great,
  input  A,
  input  B,
  input  [3:0] selector,
  output result,
  output carryOut_Great,
  output carryOut_less,
  output carryOut,
  output carryOut_inv
);

  wire and_1_out, n1_bit_adder_1_sum, n1_bit_adder_3_sum, n1_bit_adder_4_sum, not_1_out, not_2_out,
       not_3_out, not_4_out, not_5_out, or_1_out;

  not not_1 (not_1_out, B);
  _1_bit_adder u_1_bit_adder_1 (.a(A), .b(B), .carryIn(carryIn), .carryOut(carryOut), .sum(n1_bit_adder_1_sum));
  _1_bit_adder u_1_bit_adder_2 (.a(A), .b(not_1_out), .carryIn(carryIn_less), .carryOut(carryOut_less));  // open: sum
  not not_2 (not_2_out, B);
  and and_1 (and_1_out, A, B);
  or or_1 (or_1_out, A, B);
  not not_3 (not_3_out, A);
  _1_bit_adder u_1_bit_adder_3 (
    .a(not_4_out), .b(1'b0), .carryIn(carryIn_inv), .carryOut(carryOut_inv), .sum(n1_bit_adder_3_sum));
  not not_4 (not_4_out, A);
  _1_bit_adder u_1_bit_adder_4 (.a(A), .b(not_2_out), .carryIn(1'b1), .sum(n1_bit_adder_4_sum));  // open: carryOut
  not not_5 (not_5_out, A);
  _1_bit_adder u_1_bit_adder_5 (.a(not_5_out), .b(B), .carryIn(carryIn_Great), .carryOut(carryOut_Great));  // open: sum
  Multiplexer #(.select(4)) multiplexer_1 (
    .in0(1'b0), .in1(and_1_out), .in2(or_1_out), .in3(not_3_out), .in4(n1_bit_adder_1_sum),
    .in5(n1_bit_adder_3_sum), .in6(1'b0), .in7(1'b0), .in8(n1_bit_adder_4_sum), .out(result), .sel(selector));  // open: in9, in10, in11, in12, in13, in14, in15, en
endmodule

module _1_bit_ALU_MSB (
  input  carryIn_less,
  input  carryIn,
  input  carryIn_inv,
  input  carryIn_Great,
  input  A,
  input  B,
  input  [3:0] selector,
  output result,
  output overflow,
  output set_less
);

  wire and_1_out, and_2_out, and_3_out, and_4_out, and_5_out, n1_bit_adder_1_carryout, n1_bit_adder_1_sum,
       n1_bit_adder_2_sum, n1_bit_adder_3_carryout, n1_bit_adder_3_sum, n1_bit_adder_4_sum,
       n1_bit_adder_5_sum, not_1_out, not_2_out, not_3_out, not_4_out, not_5_out, not_6_out, not_7_out,
       or_1_out, or_2_out;

  not not_1 (not_1_out, B);
  _1_bit_adder u_1_bit_adder_1 (
    .a(A), .b(B), .carryIn(carryIn), .carryOut(n1_bit_adder_1_carryout), .sum(n1_bit_adder_1_sum));
  _1_bit_adder u_1_bit_adder_2 (
    .a(A), .b(not_1_out), .carryIn(carryIn_less), .sum(n1_bit_adder_2_sum));  // open: carryOut
  not not_2 (not_2_out, B);
  and and_1 (and_1_out, ~A, B);  // AND_Gate
  and and_2 (and_2_out, A, B);
  or or_1 (or_1_out, A, B);
  not not_3 (not_3_out, A);
  not not_4 (not_4_out, A);
  _1_bit_adder u_1_bit_adder_3 (
    .a(not_4_out), .b(1'b0), .carryIn(carryIn_inv), .carryOut(n1_bit_adder_3_carryout),
    .sum(n1_bit_adder_3_sum));
  _1_bit_adder u_1_bit_adder_4 (.a(A), .b(not_2_out), .carryIn(1'b1), .sum(n1_bit_adder_4_sum));  // open: carryOut
  or or_2 (or_2_out, n1_bit_adder_1_carryout, carryIn);
  not not_5 (not_5_out, and_1_out);
  and and_3 (and_3_out, n1_bit_adder_2_sum, not_5_out);
  Multiplexer multiplexer_1 (.in0(and_3_out), .in1(and_5_out), .out(set_less), .sel(selector[0]));  // open: en
  _1_bit_adder u_1_bit_adder_5 (
    .a(not_6_out), .b(B), .carryIn(carryIn_Great), .sum(n1_bit_adder_5_sum));  // open: carryOut
  not not_6 (not_6_out, A);
  and and_4 (and_4_out, A, ~B);  // AND_Gate
  not not_7 (not_7_out, and_4_out);
  and and_5 (and_5_out, not_7_out, n1_bit_adder_5_sum);
  Multiplexer #(.select(4)) multiplexer_2 (
    .in0(1'b0), .in1(and_2_out), .in2(or_1_out), .in3(not_3_out), .in4(n1_bit_adder_1_sum),
    .in5(n1_bit_adder_3_sum), .in6(1'b0), .in7(1'b0), .in8(n1_bit_adder_4_sum), .out(result), .sel(selector));  // open: in9, in10, in11, in12, in13, in14, in15, en
  Multiplexer #(.select(4)) multiplexer_3 (
    .in0(1'b0), .in1(1'b0), .in2(1'b0), .in3(1'b0), .in4(or_2_out), .in5(n1_bit_adder_3_carryout),
    .in6(1'b0), .in7(1'b0), .in8(1'b0), .in9(1'b0), .out(overflow), .sel(selector));  // open: in10, in11, in12, in13, in14, in15, en
endmodule

module _1_bit_adder (
  input  carryIn,
  input  a,
  input  b,
  output sum,
  output carryOut
);

  wire and_1_out, and_2_out, and_3_out, and_4_out, and_5_out, and_6_out, and_7_out, not_1_out, not_2_out,
       not_3_out;

  and and_1 (and_1_out, b, carryIn);
  and and_2 (and_2_out, b, a);
  and and_3 (and_3_out, a, carryIn);
  or or_1 (carryOut, and_1_out, and_2_out, and_3_out);
  not not_1 (not_1_out, carryIn);
  not not_2 (not_2_out, a);
  not not_3 (not_3_out, b);
  and and_4 (and_4_out, not_2_out, b, not_1_out);
  and and_5 (and_5_out, a, not_3_out, not_1_out);
  and and_6 (and_6_out, not_3_out, not_2_out, carryIn);
  and and_7 (and_7_out, carryIn, a, b);
  or or_2 (sum, and_7_out, and_6_out, and_4_out, and_5_out);
endmodule
