// Logisim project Project2.circ as structural Verilog: 8 circuits, main circuit 3-Bit Decoder
module _3_Bit_Decoder (
  input  [2:0] Input,
  output Out0,
  output Out1,
  output Out2,
  output Out3,
  output Out4,
  output Out5,
  output Out6,
  output Out7
);

  wire not_1_out, not_2_out, not_3_out, not_4_out, not_5_out, not_6_out, not_7_out, not_8_out, not_9_out,
       not_10_out, not_11_out, not_12_out;

  not not_1 (not_1_out, Input[0]);
  not not_2 (not_2_out, Input[1]);
  not not_3 (not_3_out, Input[2]);
  not not_4 (not_4_out, Input[1]);
  not not_5 (not_5_out, Input[2]);
  not not_6 (not_6_out, Input[0]);
  not not_7 (not_7_out, Input[2]);
  not not_8 (not_8_out, Input[2]);
  not not_9 (not_9_out, Input[0]);
  not not_10 (not_10_out, Input[1]);
  not not_11 (not_11_out, Input[1]);
  not not_12 (not_12_out, Input[0]);
  and and_1 (Out0, not_1_out, not_2_out, not_3_out);
  and and_2 (Out1, Input[0], not_4_out, not_5_out);
  and and_3 (Out2, not_6_out, Input[1], not_7_out);
  and and_4 (Out3, Input[0], Input[1], not_8_out);
  and and_5 (Out4, not_9_out, not_10_out, Input[2]);
  and and_6 (Out5, Input[0], not_11_out, Input[2]);
  and and_7 (Out6, not_12_out, Input[1], Input[2]);
  and and_8 (Out7, Input[0], Input[1], Input[2]);
endmodule

module _2_Bit_Decoder (
  input  [1:0] Input,
  output Out0,
  output Out1,
  output Out2,
  output Out3
);

  wire not_1_out, not_2_out, not_3_out, not_4_out;

  not not_1 (not_1_out, Input[0]);
  and and_1 (Out0, not_1_out, not_2_out);
  not not_2 (not_2_out, Input[1]);
  and and_2 (Out1, Input[0], not_3_out);
  not not_3 (not_3_out, Input[1]);
  not not_4 (not_4_out, Input[0]);
  and and_3 (Out2, not_4_out, Input[1]);
  and and_4 (Out3, Input[0], Input[1]);
endmodule

module _3_Bit_Multiplexer (
  input  [2:0] Input0,
  input  [2:0] Input1,
  input  [2:0] Input2,
  input  [2:0] Input3,
  input  [2:0] Input4,
  input  [2:0] Input5,
  input  [2:0] Input6,
  input  [2:0] Input7,
  input  [2:0] Selector,
  output [2:0] Output
);

  wire [2:0] and_1_out, and_2_out, and_3_out, and_4_out, and_5_out, and_6_out, and_7_out, and_8_out;
  wire [2:2] n3_bit_decoder_1_out0, n3_bit_decoder_1_out1, n3_bit_decoder_1_out2, n3_bit_decoder_1_out3,
       n3_bit_decoder_1_out4, n3_bit_decoder_1_out5, n3_bit_decoder_1_out6, n3_bit_decoder_1_out7;

  _3_Bit_Decoder u_3_bit_decoder_1 (
    .Input(Selector), .Out0(n3_bit_decoder_1_out0[2]), .Out1(n3_bit_decoder_1_out1[2]),
    .Out2(n3_bit_decoder_1_out2[2]), .Out3(n3_bit_decoder_1_out3[2]), .Out4(n3_bit_decoder_1_out4[2]),
    .Out5(n3_bit_decoder_1_out5[2]), .Out6(n3_bit_decoder_1_out6[2]), .Out7(n3_bit_decoder_1_out7[2]));
  assign and_1_out = Input0 & {3{n3_bit_decoder_1_out0[2]}};  // AND_Gate and_1, 3 bits wide
  assign and_2_out = Input1 & {3{n3_bit_decoder_1_out1[2]}};  // AND_Gate and_2, 3 bits wide
  assign and_3_out = Input2 & {3{n3_bit_decoder_1_out2[2]}};  // AND_Gate and_3, 3 bits wide
  assign and_4_out = Input3 & {3{n3_bit_decoder_1_out3[2]}};  // AND_Gate and_4, 3 bits wide
  assign and_5_out = Input4 & {3{n3_bit_decoder_1_out4[2]}};  // AND_Gate and_5, 3 bits wide
  assign and_6_out = Input5 & {3{n3_bit_decoder_1_out5[2]}};  // AND_Gate and_6, 3 bits wide
  assign and_7_out = Input6 & {3{n3_bit_decoder_1_out6[2]}};  // AND_Gate and_7, 3 bits wide
  assign and_8_out = Input7 & {3{n3_bit_decoder_1_out7[2]}};  // AND_Gate and_8, 3 bits wide
  assign Output = and_1_out | and_2_out | and_3_out | and_4_out | and_5_out | and_6_out | and_7_out | and_8_out;  // OR_Gate or_1, 3 bits wide
endmodule

module _2_Bit_Multiplexer (
  input  [1:0] Input0,
  input  [1:0] Input1,
  input  [1:0] Input2,
  input  [1:0] Input3,
  input  [1:0] Selector,
  output [1:0] Output
);

  wire [1:0] and_1_out, and_2_out, and_3_out, and_4_out;
  wire [1:1] n2_bit_decoder_1_out0, n2_bit_decoder_1_out1, n2_bit_decoder_1_out2, n2_bit_decoder_1_out3;

  _2_Bit_Decoder u_2_bit_decoder_1 (
    .Input(Selector), .Out0(n2_bit_decoder_1_out0[1]), .Out1(n2_bit_decoder_1_out1[1]),
    .Out2(n2_bit_decoder_1_out2[1]), .Out3(n2_bit_decoder_1_out3[1]));
  assign and_1_out = Input0 & {2{n2_bit_decoder_1_out0[1]}};  // AND_Gate and_1, 2 bits wide
  assign and_2_out = Input1 & {2{n2_bit_decoder_1_out1[1]}};  // AND_Gate and_2, 2 bits wide
  assign and_3_out = Input2 & {2{n2_bit_decoder_1_out2[1]}};  // AND_Gate and_3, 2 bits wide
  assign and_4_out = Input3 & {2{n2_bit_decoder_1_out3[1]}};  // AND_Gate and_4, 2 bits wide
  assign Output = and_1_out | and_2_out | and_3_out | and_4_out;  // OR_Gate or_1, 2 bits wide
endmodule

module _1_Bit_Adder (
  input  CarryIn,
  input  A,
  input  B,
  output Output,
  output CarryOut
);

  wire and_1_out, and_2_out, and_3_out, and_4_out, and_5_out, and_6_out, and_7_out, not_1_out, not_2_out,
       not_3_out, not_4_out, not_5_out, not_6_out;

  and and_1 (and_1_out, B, CarryIn);
  and and_2 (and_2_out, A, CarryIn);
  or or_1 (CarryOut, and_1_out, and_2_out, and_7_out);
  not not_1 (not_1_out, B);
  and and_3 (and_3_out, A, not_1_out, not_2_out);
  not not_2 (not_2_out, CarryIn);
  not not_3 (not_3_out, A);
  and and_4 (and_4_out, not_3_out, B, not_4_out);
  not not_4 (not_4_out, CarryIn);
  not not_5 (not_5_out, A);
  not not_6 (not_6_out, B);
  and and_5 (and_5_out, not_5_out, not_6_out, CarryIn);
  and and_6 (and_6_out, A, B, CarryIn);
  and and_7 (and_7_out, B, A);
  or or_2 (Output, and_3_out, and_4_out, and_5_out, and_6_out);
endmodule

module _16_Bit_Adder (
  input  in_1,
  input  [15:0] in_2,
  input  [15:0] in_3,
  output [15:0] out_4,
  output OverFlow
);

  wire n1_bit_adder_1_carryout, n1_bit_adder_2_carryout, n1_bit_adder_3_carryout, n1_bit_adder_4_carryout,
       n1_bit_adder_5_carryout, n1_bit_adder_6_carryout, n1_bit_adder_7_carryout, n1_bit_adder_8_carryout,
       n1_bit_adder_9_carryout, n1_bit_adder_10_carryout, n1_bit_adder_11_carryout, n1_bit_adder_12_carryout,
       n1_bit_adder_13_carryout, n1_bit_adder_14_carryout, n1_bit_adder_15_carryout;

  _1_Bit_Adder u_1_bit_adder_1 (
    .A(in_2[0]), .B(in_3[0]), .CarryIn(in_1), .CarryOut(n1_bit_adder_1_carryout), .Output(out_4[0]));
  _1_Bit_Adder u_1_bit_adder_2 (
    .A(in_2[1]), .B(in_3[1]), .CarryIn(n1_bit_adder_1_carryout), .CarryOut(n1_bit_adder_2_carryout),
    .Output(out_4[1]));
  _1_Bit_Adder u_1_bit_adder_3 (
    .A(in_2[2]), .B(in_3[2]), .CarryIn(n1_bit_adder_2_carryout), .CarryOut(n1_bit_adder_3_carryout),
    .Output(out_4[2]));
  _1_Bit_Adder u_1_bit_adder_4 (
    .A(in_2[3]), .B(in_3[3]), .CarryIn(n1_bit_adder_3_carryout), .CarryOut(n1_bit_adder_4_carryout),
    .Output(out_4[3]));
  _1_Bit_Adder u_1_bit_adder_5 (
    .A(in_2[4]), .B(in_3[4]), .CarryIn(n1_bit_adder_4_carryout), .CarryOut(n1_bit_adder_5_carryout),
    .Output(out_4[4]));
  _1_Bit_Adder u_1_bit_adder_6 (
    .A(in_2[5]), .B(in_3[5]), .CarryIn(n1_bit_adder_5_carryout), .CarryOut(n1_bit_adder_6_carryout),
    .Output(out_4[5]));
  _1_Bit_Adder u_1_bit_adder_7 (
    .A(in_2[6]), .B(in_3[6]), .CarryIn(n1_bit_adder_6_carryout), .CarryOut(n1_bit_adder_7_carryout),
    .Output(out_4[6]));
  _1_Bit_Adder u_1_bit_adder_8 (
    .A(in_2[7]), .B(in_3[7]), .CarryIn(n1_bit_adder_7_carryout), .CarryOut(n1_bit_adder_8_carryout),
    .Output(out_4[7]));
  _1_Bit_Adder u_1_bit_adder_9 (
    .A(in_2[8]), .B(in_3[8]), .CarryIn(n1_bit_adder_8_carryout), .CarryOut(n1_bit_adder_9_carryout),
    .Output(out_4[8]));
  _1_Bit_Adder u_1_bit_adder_10 (
    .A(in_2[9]), .B(in_3[9]), .CarryIn(n1_bit_adder_9_carryout), .CarryOut(n1_bit_adder_10_carryout),
    .Output(out_4[9]));
  _1_Bit_Adder u_1_bit_adder_11 (
    .A(in_2[10]), .B(in_3[10]), .CarryIn(n1_bit_adder_10_carryout), .CarryOut(n1_bit_adder_11_carryout),
    .Output(out_4[10]));
  _1_Bit_Adder u_1_bit_adder_12 (
    .A(in_2[11]), .B(in_3[11]), .CarryIn(n1_bit_adder_11_carryout), .CarryOut(n1_bit_adder_12_carryout),
    .Output(out_4[11]));
  _1_Bit_Adder u_1_bit_adder_13 (
    .A(in_2[12]), .B(in_3[12]), .CarryIn(n1_bit_adder_12_carryout), .CarryOut(n1_bit_adder_13_carryout),
    .Output(out_4[12]));
  _1_Bit_Adder u_1_bit_adder_14 (
    .A(in_2[13]), .B(in_3[13]), .CarryIn(n1_bit_adder_13_carryout), .CarryOut(n1_bit_adder_14_carryout),
    .Output(out_4[13]));
  _1_Bit_Adder u_1_bit_adder_15 (
    .A(in_2[14]), .B(in_3[14]), .CarryIn(n1_bit_adder_14_carryout), .CarryOut(n1_bit_adder_15_carryout),
    .Output(out_4[14]));
  _1_Bit_Adder u_1_bit_adder_16 (
    .A(in_2[15]), .B(in_3[15]), .CarryIn(n1_bit_adder_15_carryout), .CarryOut(OverFlow), .Output(out_4[15]));
endmodule

module _4_bit_Abstraction__CLA (
  input  [3:0] A,
  input  in_2,
  input  [3:0] B,
  output s0,
  output s1,
  output s2,
  output s3,
  output P,
  output G
);

  wire and_5_out, and_6_out, and_7_out, and_8_out, and_9_out, and_10_out, and_11_out, and_12_out, and_13_out,
       and_14_out, and_16_out, and_17_out, and_18_out, c1, c2, c3, c4, g0, g1, g2, g3, p0, p1, p2, p3;

  and and_1 (g0, A[0], B[0]);
  or or_1 (p0, A[0], B[0]);
  and and_2 (g1, A[1], B[1]);
  or or_2 (p1, A[1], B[1]);
  and and_3 (g2, A[2], B[2]);
  or or_3 (p2, A[2], B[2]);
  and and_4 (g3, A[3], B[3]);
  or or_4 (p3, A[3], B[3]);
  and and_5 (and_5_out, in_2, p0);
  and and_6 (and_6_out, g0, p1);
  and and_7 (and_7_out, p0, p1, in_2);
  and and_8 (and_8_out, p2, g1);
  and and_9 (and_9_out, p2, p1, g0);
  and and_10 (and_10_out, p2, p1, p0, in_2);
  and and_11 (and_11_out, p3, g2);
  and and_12 (and_12_out, p3, p2, g1);
  and and_13 (and_13_out, p3, p2, p1, g0);
  and and_14 (and_14_out, p3, p2, p2, p1, in_2);
  or or_5 (c1, g0, and_5_out);
  or or_6 (c2, and_6_out, g1, and_7_out);
  or or_7 (c3, g2, and_8_out, and_9_out, and_10_out);
  or or_8 (c4, g3, and_11_out, and_12_out, and_13_out, and_14_out);
  and and_15 (P, p0, p1, p2, p3);
  _1_Bit_Adder u_1_bit_adder_1 (.A(A[0]), .B(B[0]), .CarryIn(in_2), .Output(s0));  // open: CarryOut
  _1_Bit_Adder u_1_bit_adder_2 (.A(A[1]), .B(B[1]), .CarryIn(c1), .Output(s1));  // open: CarryOut
  _1_Bit_Adder u_1_bit_adder_3 (.A(A[2]), .B(B[2]), .CarryIn(c2), .Output(s2));  // open: CarryOut
  _1_Bit_Adder u_1_bit_adder_4 (.A(A[3]), .B(B[3]), .CarryIn(c3), .Output(s3));  // open: CarryOut
  and and_16 (and_16_out, p3, g2);
  and and_17 (and_17_out, p3, p2, g1);
  and and_18 (and_18_out, p3, p2, p1, g0);
  or or_9 (G, g3, and_16_out, and_17_out, and_18_out);

  // Other names for the same wires on the sheet: c0 = in_2
endmodule

module _16_Bit_Adder__CLA (
  input  CarryIn,
  input  [15:0] A,
  input  [15:0] B,
  output [15:0] Output,
  output CarryOut
);

  wire and_1_out, and_2_out, and_3_out, and_4_out, and_5_out, and_6_out, and_7_out, and_8_out, and_9_out,
       and_10_out, C1, C2, C3, G0, G1, G2, G3, P0, P1, P2, P3;

  _4_bit_Abstraction__CLA u_4_bit_abstraction_cla_1 (
    .A(A[3:0]), .B(B[3:0]), .in_2(CarryIn), .P(P0), .G(G0), .s0(Output[0]), .s1(Output[1]), .s2(Output[2]),
    .s3(Output[3]));
  _4_bit_Abstraction__CLA u_4_bit_abstraction_cla_2 (
    .A(A[7:4]), .B(B[7:4]), .in_2(C1), .P(P1), .G(G1), .s0(Output[4]), .s1(Output[5]), .s2(Output[6]),
    .s3(Output[7]));
  _4_bit_Abstraction__CLA u_4_bit_abstraction_cla_3 (
    .A(A[11:8]), .B(B[11:8]), .in_2(C2), .P(P2), .G(G2), .s0(Output[8]), .s1(Output[9]), .s2(Output[10]),
    .s3(Output[11]));
  _4_bit_Abstraction__CLA u_4_bit_abstraction_cla_4 (
    .A(A[15:12]), .B(B[15:12]), .in_2(C3), .P(P3), .G(G3), .s0(Output[12]), .s1(Output[13]), .s2(Output[14]),
    .s3(Output[15]));
  and and_1 (and_1_out, CarryIn, P0);
  and and_2 (and_2_out, G0, P1);
  and and_3 (and_3_out, P0, P1, CarryIn);
  and and_4 (and_4_out, P2, G1);
  and and_5 (and_5_out, P2, P1, G0);
  and and_6 (and_6_out, P2, P1, P0, CarryIn);
  and and_7 (and_7_out, P3, G2);
  and and_8 (and_8_out, P3, P2, G1);
  and and_9 (and_9_out, P3, P2, P1, G0);
  and and_10 (and_10_out, P3, P2, P1, P0, CarryIn);
  or or_1 (C1, G0, and_1_out);
  or or_2 (C2, and_2_out, G1, and_3_out);
  or or_3 (C3, G2, and_4_out, and_5_out, and_6_out);
  or or_4 (CarryOut, G3, and_7_out, and_8_out, and_9_out, and_10_out);

  // Other names for the same wires on the sheet: a0[3:0] = A[3:0]; a1[3:0] = A[7:4]; a2[3:0] = A[11:8];
  //   a3[3:0] = A[15:12]; b0[3:0] = B[3:0]; b1[3:0] = B[7:4]; b2[3:0] = B[11:8]; b3[3:0] = B[15:12]; C4 = CarryOut
endmodule
