// Logisim project SD_Group29v7.circ as structural Verilog: 5 circuits, main circuit main
module main (
  input  [15:0] Branch_Value,
  output [15:0] pc,
  output [15:0] r0,
  output [15:0] r1,
  output [15:0] r2,
  output [15:0] r3,
  output [15:0] r4,
  output [15:0] r5,
  output [15:0] r6,
  output [15:0] r7,
  output [15:0] r8,
  output [15:0] r9,
  output [15:0] r10,
  output [15:0] r11,
  output [15:0] r12,
  output [15:0] r13,
  output [15:0] r14,
  output [15:0] r15,
  output halt
);

  wire bne, bne_control, C, clock_1_out, comparator_1_gt, comparator_1_lt, jal, jr, LD, load_store, lui,
       or_1_out, or_2_out, or_3_out, or_5_out, ori_lui, Reset, str, writeEnabled;
  wire [3:0] multiplexer_4_out, multiplexer_9_out, multiplexer_10_out, multiplexer_11_out, OPCODE;
  wire [7:0] ram_1_data_2;
  wire [11:8] ram_1_data;
  wire [15:0] adder_1_out, adder_2_out, adder_3_out, adder_4_out, bit_extender_1_out, bit_extender_2_out,
       bit_extender_3_out, bit_extender_4_out, bit_extender_5_out, multiplexer_1_out, multiplexer_2_out,
       multiplexer_3_out, multiplexer_5_out, multiplexer_6_out, multiplexer_7_out, multiplexer_8_out,
       multiplexer_12_out, multiplexer_13_out, n16_bit_adder_cla_1_output, n16_bit_alu_1_result, or_4_out,
       ori_lui_8bit, ram_2_data, register_file_for_datapath_1_s, register_file_for_datapath_1_t;

  Halt halt_1 (.instruction({OPCODE, ram_1_data, ram_1_data_2}), .clock(clock_1_out), .reset(Reset), .halt(halt));
  Clock clock_1 (.out(clock_1_out));
  Button u_reset (.out(Reset));
  and and_1 (C, ~halt, clock_1_out);  // AND_Gate
  Multiplexer #(.width(16)) multiplexer_1 (
    .in0(16'h1), .in1(multiplexer_3_out), .out(multiplexer_1_out), .sel(bne));  // open: en
  _16_Bit_Adder__CLA u_16_bit_adder_cla_1 (
    .A(multiplexer_1_out), .B(pc), .CarryIn(1'b0), .Output(n16_bit_adder_cla_1_output));  // open: CarryOut
  or or_1 (or_1_out, jal, jr);
  Multiplexer #(.width(16)) multiplexer_2 (
    .in0(n16_bit_adder_cla_1_output), .in1(multiplexer_3_out), .out(multiplexer_2_out), .sel(or_1_out));  // open: en
  _16bit_Register _16Bit_Register (.C(C), .D(multiplexer_2_out), .Write_Enabled(1'b1), .Reset(Reset), .Q(pc));
  Multiplexer #(.width(16)) multiplexer_3 (
    .in0(multiplexer_5_out), .in1(adder_1_out), .out(multiplexer_3_out), .sel(bne));  // open: en
  assign bit_extender_1_out = {{8{1'b0}}, ram_1_data_2};  // Bit_Extender bit_extender_1
  Multiplexer #(.width(4)) multiplexer_4 (
    .in0(4'b0000), .in1(4'b1000), .out(multiplexer_4_out), .sel(lui));  // open: en
  Multiplexer #(.width(16)) multiplexer_5 (
    .in0(bit_extender_4_out), .in1(adder_3_out), .out(multiplexer_5_out), .sel(jr));  // open: en
  Shifter #(.width(16)) shifter_1 (.in(bit_extender_1_out), .\dist (multiplexer_4_out), .out(ori_lui_8bit));
  RAM #(.addrWidth(16), .dataWidth(16)) ram_1 (
    .addr(pc), .data({OPCODE, ram_1_data, ram_1_data_2}));  // open: sel, clk, ld, clr
  assign bit_extender_2_out = {{12{ram_1_data_2[3]}}, ram_1_data_2[3:0]};  // Bit_Extender bit_extender_2
  Adder #(.width(16)) adder_1 (.a(16'h1), .b(bit_extender_2_out), .out(adder_1_out));  // open: cin, cout
  assign bit_extender_3_out = {{8{1'b0}}, ram_1_data_2};  // Bit_Extender bit_extender_3
  assign bit_extender_4_out = {{4{1'b0}}, {ram_1_data, ram_1_data_2}};  // Bit_Extender bit_extender_4
  Multiplexer #(.width(16)) multiplexer_6 (
    .in0(multiplexer_12_out), .in1(multiplexer_7_out), .out(multiplexer_6_out), .sel(ori_lui));  // open: en
  Adder #(.width(16)) adder_2 (.a(pc), .b(16'h1), .out(adder_2_out));  // open: cin, cout
  buf or_2 (or_2_out, load_store);  // OR_Gate
  Adder #(.width(16)) adder_3 (
    .a(bit_extender_3_out), .b(register_file_for_datapath_1_t), .out(adder_3_out));  // open: cin, cout
  Multiplexer #(.width(16)) multiplexer_7 (
    .in0(or_4_out), .in1(ori_lui_8bit), .out(multiplexer_7_out), .sel(lui));  // open: en
  Multiplexer #(.width(16)) multiplexer_8 (
    .in0(multiplexer_6_out), .in1(adder_2_out), .out(multiplexer_8_out), .sel(jal));  // open: en
  Multiplexer #(.width(4)) multiplexer_9 (
    .in0(ram_1_data), .in1(ram_1_data_2[7:4]), .out(multiplexer_9_out), .sel(or_2_out));  // open: en
  controlUnit controlunit_1 (
    .OPCODE(OPCODE), .writeenqbled(writeEnabled), .LD(LD), .str(str), .load_store(load_store), .jal(jal),
    .ori_lui(ori_lui), .lui(lui), .jr(jr), .bne(bne_control));
  Multiplexer #(.width(4)) multiplexer_10 (
    .in0(multiplexer_9_out), .in1(4'b1111), .out(multiplexer_10_out), .sel(jal));  // open: en
  or or_3 (or_3_out, load_store, jr, ori_lui, bne_control);
  assign or_4_out = ori_lui_8bit | register_file_for_datapath_1_t;  // OR_Gate or_4, 16 bits wide
  Register_File_for_DataPath register_file_for_datapath_1 (
    .Reset(Reset), .Write(writeEnabled), .clock(C), .Data(multiplexer_8_out), .rs(ram_1_data_2[7:4]),
    .rd(multiplexer_10_out), .rt(multiplexer_11_out), .r0(r0), .r8(r8), .r1(r1), .r9(r9), .r2(r2), .r10(r10),
    .r3(r3), .r11(r11), .r4(r4), .r12(r12), .r5(r5), .r13(r13), .r6(r6), .r14(r14), .r7(r7), .r15(r15),
    .S(register_file_for_datapath_1_s), .T(register_file_for_datapath_1_t));
  Multiplexer #(.width(4)) multiplexer_11 (
    .in0(ram_1_data_2[3:0]), .in1(ram_1_data), .out(multiplexer_11_out), .sel(or_3_out));  // open: en
  assign bit_extender_5_out = {{12{1'b0}}, ram_1_data_2[3:0]};  // Bit_Extender bit_extender_5
  Adder #(.width(16)) adder_4 (
    .a(bit_extender_5_out), .b(register_file_for_datapath_1_t), .out(adder_4_out));  // open: cin, cout
  _16_bit_ALU u_16_bit_alu_1 (
    .opcode(OPCODE), .a(register_file_for_datapath_1_s), .b(register_file_for_datapath_1_t),
    .result(n16_bit_alu_1_result));  // open: overflow, zero
  Comparator #(.width(16)) comparator_1 (
    .a(register_file_for_datapath_1_s), .b(register_file_for_datapath_1_t), .gt(comparator_1_gt),
    .lt(comparator_1_lt));  // open: eq
  Multiplexer #(.width(16)) multiplexer_12 (
    .in0(n16_bit_alu_1_result), .in1(ram_2_data), .out(multiplexer_12_out), .sel(load_store));  // open: en
  or or_5 (or_5_out, comparator_1_gt, comparator_1_lt);
  Multiplexer #(.width(16)) multiplexer_13 (
    .in0(n16_bit_alu_1_result), .in1(adder_4_out), .out(multiplexer_13_out), .sel(load_store));  // open: en
  and and_2 (bne, or_5_out, bne_control);
  RAM #(.addrWidth(16), .dataWidth(16), .bus("separate")) ram_2 (
    .addr(multiplexer_13_out), .din(register_file_for_datapath_1_s), .data(ram_2_data), .str(str), .clk(C),
    .ld(LD));  // open: sel, clr

  // Notes on the sheet:
  //   CLA
  //   DO NOT CHANGE THE INPUTS AND OUTPUTS OF THIS CIRCUIT! Do not add/remove inputs or outputs. Do not even change their location or orientation.
  //   RT
  //   RS
  //   RD
endmodule

module Halt (
  input  [15:0] instruction,
  input  clock,
  input  reset,
  output halt
);

  wire and_1_out, comparator_1_eq, comparator_2_gt, counter_1_carry, or_1_out, or_2_out;
  wire [15:0] counter_1_q;

  Comparator #(.width(16), .mode("unsigned")) comparator_1 (
    .a(instruction), .b({16{1'b0}}), .eq(comparator_1_eq));  // open: gt, lt
  Counter #(.width(16), .max('hffff), .trigger("falling")) counter_1 (
    .Q(counter_1_q), .carry(counter_1_carry), .clk(clock), .clr(reset));  // open: load, D, count
  or or_1 (or_1_out, comparator_1_eq, counter_1_carry);
  Comparator #(.width(16), .mode("unsigned")) comparator_2 (
    .a(counter_1_q), .b({16{1'b0}}), .gt(comparator_2_gt));  // open: eq, lt
  or or_2 (or_2_out, halt, and_1_out);
  and and_1 (and_1_out, or_1_out, comparator_2_gt);
  Register #(.width(1)) register_1 (.D(or_2_out), .Q(halt), .clk(clock), .clr(reset));  // open: en

  // Notes on the sheet:
  //   halt becomes and stays asserted if the instruction is 0000 (not in the first clock cycle) or the end of the counter is reached (2^16)
endmodule

module _16Bit_Program_Counter (
  input  [15:0] Branch_Value,
  input  Branch_Relative,
  input  Reset,
  input  Branche_Absolute,
  input  Clock,
  output [15:0] out_6
);

  wire [15:0] multiplexer_1_out, multiplexer_2_out, n16_bit_adder_cla_1_output;

  Multiplexer #(.width(16)) multiplexer_1 (
    .in0(16'h1), .in1(Branch_Value), .out(multiplexer_1_out), .sel(Branch_Relative));  // open: en
  _16_Bit_Adder__CLA u_16_bit_adder_cla_1 (
    .A(multiplexer_1_out), .B(out_6), .CarryIn(1'b0), .Output(n16_bit_adder_cla_1_output));  // open: CarryOut
  Multiplexer #(.width(16)) multiplexer_2 (
    .in0(n16_bit_adder_cla_1_output), .in1(Branch_Value), .out(multiplexer_2_out), .sel(Branche_Absolute));  // open: en
  _16bit_Register _16Bit_Register (.C(Clock), .D(multiplexer_2_out), .Write_Enabled(1'b1), .Reset(Reset), .Q(out_6));

  // Notes on the sheet:
  //   CLA
endmodule

module Register_File_for_DataPath (
  input  Reset,
  input  Write,
  input  [3:0] rs,
  input  clock,
  input  [15:0] Data,
  input  [3:0] rd,
  input  [3:0] rt,
  output [15:0] r0,
  output [15:0] r8,
  output [15:0] r1,
  output [15:0] r9,
  output [15:0] r2,
  output [15:0] r10,
  output [15:0] r3,
  output [15:0] r11,
  output [15:0] r4,
  output [15:0] r12,
  output [15:0] r5,
  output [15:0] r13,
  output [15:0] r6,
  output [15:0] r14,
  output [15:0] r7,
  output [15:0] r15,
  output [15:0] S,
  output [15:0] T
);

  Register_File__WRITE register_file_write_1 (
    .Register_Data(Data), .Clockwrite(clock), .Write(Write), .Reset(Reset), .Selector(rd), .out_6(r0),
    .out_7(r1), .out_8(r2), .out_9(r3), .out_10(r4), .out_11(r5), .out_12(r6), .out_13(r7), .out_14(r8),
    .out_15(r9), .out_16(r10), .out_17(r11), .out_18(r12), .out_19(r13), .out_20(r14), .out_21(r15));
  Register_File__READ register_file_read_1 (
    .Read_1(rs), .in_2(r0), .in_3(r1), .in_4(r2), .in_5(r3), .in_6(r4), .in_7(r5), .in_8(r6), .in_9(r7),
    .in_10(r8), .in_11(r9), .in_12(r10), .in_13(r11), .in_14(r12), .in_15(r13), .in_16(r14), .in_17(r15),
    .Read_2(rt), .Data_1(S), .Data_2(T));

  // Notes on the sheet:
  //   WRITE
  //   READ
endmodule

module controlUnit (
  input  [3:0] OPCODE,
  output writeenqbled,
  output LD,
  output str,
  output load_store,
  output jal,
  output ori_lui,
  output lui,
  output jr,
  output bne
);

  wire and_4_out, and_6_out;

  and and_1 (jr, OPCODE[3], OPCODE[2], ~OPCODE[1], ~OPCODE[0]);  // AND_Gate
  and and_2 (bne, OPCODE[3], OPCODE[2], ~OPCODE[1], OPCODE[0]);  // AND_Gate
  and and_3 (jal, OPCODE[3], ~OPCODE[2], ~OPCODE[1], OPCODE[0]);  // AND_Gate
  and and_4 (and_4_out, OPCODE[3], OPCODE[2], OPCODE[1], ~OPCODE[0]);  // AND_Gate
  and and_5 (str, OPCODE[3], OPCODE[2], OPCODE[1], OPCODE[0]);
  and and_6 (and_6_out, OPCODE[3], ~OPCODE[2], OPCODE[1], ~OPCODE[0]);  // AND_Gate
  and and_7 (lui, OPCODE[3], ~OPCODE[2], OPCODE[1], OPCODE[0]);  // AND_Gate
  or or_1 (ori_lui, and_6_out, lui);
  not not_1 (writeenqbled, bne);
  or or_2 (LD, str, and_4_out);
  or or_3 (load_store, and_4_out, str);
endmodule
