// Logisim project SD_Group29v7CleanUp.circ as structural Verilog: 6 circuits, main circuit main
module main (
  input  [15:0] Branch_Value,
  output [15:0] pc,
  output [15:0] r0,
  output [15:0] r1,
  output [15:0] r2,
  output [15:0] r3,
  output [15:0] r4,
  output [15:0] r5,
  output [15:0] r6,
  output [15:0] r7,
  output [15:0] r8,
  output [15:0] r9,
  output [15:0] r10,
  output [15:0] r11,
  output [15:0] r12,
  output [15:0] r13,
  output [15:0] r14,
  output [15:0] r15,
  output halt
);

  wire bne, bne_control, C, clock_1_out, comparator_1_gt, comparator_1_lt, jal, jr, LD, load_store, lui,
       or_1_out, or_2_out, or_4_out, ori_lui, Reset, STR, writeEnabled;
  wire [3:0] ALU_OPCODE, multiplexer_3_out, multiplexer_7_out, multiplexer_10_out, multiplexer_11_out;
  wire [15:0] adder_1_out, adder_2_out, adder_3_out, Immediate, Instruction, multiplexer_1_out,
       multiplexer_2_out, multiplexer_4_out, multiplexer_5_out, multiplexer_6_out, multiplexer_8_out,
       multiplexer_9_out, multiplexer_12_out, multiplexer_13_out, n16_bit_adder_cla_1_output,
       n16_bit_alu_1_result, or_3_out, ori_lui_8bit, ram_2_data, reg___imm, register_file_for_datapath_1_s,
       register_file_for_datapath_1_t;

  Halt halt_1 (.instruction(Instruction), .clock(clock_1_out), .reset(Reset), .halt(halt));
  Clock clock_1 (.out(clock_1_out));
  Button u_reset (.out(Reset));
  and and_1 (C, ~halt, clock_1_out);  // AND_Gate
  Multiplexer #(.width(16)) multiplexer_1 (
    .in0(16'h1), .in1(multiplexer_4_out), .out(multiplexer_1_out), .sel(bne));  // open: en
  _16_Bit_Adder__CLA u_16_bit_adder_cla_1 (
    .A(multiplexer_1_out), .B(pc), .CarryIn(1'b0), .Output(n16_bit_adder_cla_1_output));  // open: CarryOut
  or or_1 (or_1_out, jal, jr);
  Multiplexer #(.width(16)) multiplexer_2 (
    .in0(n16_bit_adder_cla_1_output), .in1(multiplexer_4_out), .out(multiplexer_2_out), .sel(or_1_out));  // open: en
  // _16bit_Register _16Bit_Register: pin names not known; wires that end beside it: C, multiplexer_2_out, 1'b1, Reset, pc, Reset
  Multiplexer #(.width(4)) multiplexer_3 (
    .in0(4'b0000), .in1(4'b1000), .out(multiplexer_3_out), .sel(lui));  // open: en
  Adder #(.width(16)) adder_1 (.a(16'h1), .b(Immediate), .out(adder_1_out));  // open: cin, cout
  Multiplexer #(.width(16)) multiplexer_4 (
    .in0(multiplexer_5_out), .in1(adder_1_out), .out(multiplexer_4_out), .sel(bne));  // open: en
  Shifter #(.width(16)) shifter_1 (.in(Immediate), .\dist (multiplexer_3_out), .out(ori_lui_8bit));
  RAM #(.addrWidth(16), .dataWidth(16)) ram_1 (.addr(pc), .data(Instruction));  // open: sel, clk, ld, clr
  Multiplexer #(.width(16)) multiplexer_5 (
    .in0(Immediate), .in1(reg___imm), .out(multiplexer_5_out), .sel(jr));  // open: en
  Multiplexer #(.width(16)) multiplexer_6 (
    .in0(multiplexer_12_out), .in1(multiplexer_8_out), .out(multiplexer_6_out), .sel(ori_lui));  // open: en
  Adder #(.width(16)) adder_2 (.a(pc), .b(16'h1), .out(adder_2_out));  // open: cin, cout
  Multiplexer #(.width(4)) multiplexer_7 (
    .in0(Instruction[11:8]), .in1(Instruction[7:4]), .out(multiplexer_7_out), .sel(load_store));  // open: en
  Multiplexer #(.width(16)) multiplexer_8 (
    .in0(or_3_out), .in1(ori_lui_8bit), .out(multiplexer_8_out), .sel(lui));  // open: en
  controlUnit controlunit_1 (
    .Instruction(Instruction), .Immediate(Immediate), .WriteEnabled(writeEnabled), .LD__RamBlock(LD),
    .STR__RamBlock(STR), .load_store__Mux_s(load_store), .jal(jal), .ori_lui(ori_lui), .lui(lui), .jr(jr),
    .bne(bne_control), .ALU_OPCODE(ALU_OPCODE));
  Multiplexer #(.width(16)) multiplexer_9 (
    .in0(multiplexer_6_out), .in1(adder_2_out), .out(multiplexer_9_out), .sel(jal));  // open: en
  Multiplexer #(.width(4)) multiplexer_10 (
    .in0(multiplexer_7_out), .in1(4'b1111), .out(multiplexer_10_out), .sel(jal));  // open: en
  or or_2 (or_2_out, load_store, jr, ori_lui, bne_control);
  assign or_3_out = ori_lui_8bit | register_file_for_datapath_1_t;  // OR_Gate or_3, 16 bits wide
  Register_File_for_DataPath register_file_for_datapath_1 (
    .Reset(Reset), .Write(writeEnabled), .clock(C), .Data(multiplexer_9_out), .rs(Instruction[7:4]),
    .rd(multiplexer_10_out), .rt(multiplexer_11_out), .r0(r0), .r8(r8), .r1(r1), .r9(r9), .r2(r2), .r10(r10),
    .r3(r3), .r11(r11), .r4(r4), .r12(r12), .r5(r5), .r13(r13), .r6(r6), .r14(r14), .r7(r7), .r15(r15),
    .S(register_file_for_datapath_1_s), .T(register_file_for_datapath_1_t));
  Multiplexer #(.width(4)) multiplexer_11 (
    .in0(Instruction[3:0]), .in1(Instruction[11:8]), .out(multiplexer_11_out), .sel(or_2_out));  // open: en
  Adder #(.width(16)) adder_3 (
    .a(Immediate), .b(register_file_for_datapath_1_t), .out(adder_3_out));  // open: cin, cout
  _16_bit_ALU u_16_bit_alu_1 (
    .opcode(ALU_OPCODE), .a(register_file_for_datapath_1_s), .b(register_file_for_datapath_1_t),
    .result(n16_bit_alu_1_result));  // open: overflow, zero
  Comparator #(.width(16)) comparator_1 (
    .a(register_file_for_datapath_1_s), .b(register_file_for_datapath_1_t), .gt(comparator_1_gt),
    .lt(comparator_1_lt));  // open: eq
  Adder #(.width(16)) adder_4 (.a(Immediate), .b(register_file_for_datapath_1_t), .out(reg___imm));  // open: cin, cout
  Multiplexer #(.width(16)) multiplexer_12 (
    .in0(n16_bit_alu_1_result), .in1(ram_2_data), .out(multiplexer_12_out), .sel(load_store));  // open: en
  or or_4 (or_4_out, comparator_1_gt, comparator_1_lt);
  Multiplexer #(.width(16)) multiplexer_13 (
    .in0(n16_bit_alu_1_result), .in1(adder_3_out), .out(multiplexer_13_out), .sel(load_store));  // open: en
  and and_2 (bne, or_4_out, bne_control);
  RAM #(.addrWidth(16), .dataWidth(16), .bus("separate")) ram_2 (
    .addr(multiplexer_13_out), .din(register_file_for_datapath_1_s), .data(ram_2_data), .str(STR), .clk(C),
    .ld(LD));  // open: sel, clr

  // Notes on the sheet:
  //   former relative
  //   CLA
  //   former absolute
  //   To Control
  //   DO NOT CHANGE THE INPUTS AND OUTPUTS OF THIS CIRCUIT! Do not add/remove inputs or outputs. Do not even change their location or orientation.
  //   RT
  //   RS
  //   RD
  //   RT
endmodule

module Halt (
  input  [15:0] instruction,
  input  clock,
  input  reset,
  output halt
);

  wire and_1_out, comparator_1_eq, comparator_2_gt, counter_1_carry, or_1_out, or_2_out;
  wire [15:0] counter_1_q;

  Comparator #(.width(16), .mode("unsigned")) comparator_1 (
    .a(instruction), .b({16{1'b0}}), .eq(comparator_1_eq));  // open: gt, lt
  Counter #(.width(16), .max('hffff), .trigger("falling")) counter_1 (
    .Q(counter_1_q), .carry(counter_1_carry), .clk(clock), .clr(reset));  // open: load, D, count
  or or_1 (or_1_out, comparator_1_eq, counter_1_carry);
  Comparator #(.width(16), .mode("unsigned")) comparator_2 (
    .a(counter_1_q), .b({16{1'b0}}), .gt(comparator_2_gt));  // open: eq, lt
  or or_2 (or_2_out, halt, and_1_out);
  and and_1 (and_1_out, or_1_out, comparator_2_gt);
  Register #(.width(1)) register_1 (.D(or_2_out), .Q(halt), .clk(clock), .clr(reset));  // open: en

  // Notes on the sheet:
  //   halt becomes and stays asserted if the instruction is 0000 (not in the first clock cycle) or the end of the counter is reached (2^16)
endmodule

module _16Bit_Program_Counter (
  input  [15:0] Branch_Value,
  input  Branch_Relative,
  input  Reset,
  input  Branche_Absolute,
  input  Clock,
  output [15:0] out_6
);

  wire [15:0] multiplexer_1_out, multiplexer_2_out, n16_bit_adder_cla_1_output;

  Multiplexer #(.width(16)) multiplexer_1 (
    .in0(16'h1), .in1(Branch_Value), .out(multiplexer_1_out), .sel(Branch_Relative));  // open: en
  _16_Bit_Adder__CLA u_16_bit_adder_cla_1 (
    .A(multiplexer_1_out), .B(out_6), .CarryIn(1'b0), .Output(n16_bit_adder_cla_1_output));  // open: CarryOut
  Multiplexer #(.width(16)) multiplexer_2 (
    .in0(n16_bit_adder_cla_1_output), .in1(Branch_Value), .out(multiplexer_2_out), .sel(Branche_Absolute));  // open: en
  // _16bit_Register _16Bit_Register: pin names not known; wires that end beside it: Clock, multiplexer_2_out, 1'b1, Reset, out_6

  // Notes on the sheet:
  //   CLA
endmodule

module Register_File_for_DataPath (
  input  Reset,
  input  Write,
  input  [3:0] rs,
  input  clock,
  input  [15:0] Data,
  input  [3:0] rd,
  input  [3:0] rt,
  output [15:0] r0,
  output [15:0] r8,
  output [15:0] r1,
  output [15:0] r9,
  output [15:0] r2,
  output [15:0] r10,
  output [15:0] r3,
  output [15:0] r11,
  output [15:0] r4,
  output [15:0] r12,
  output [15:0] r5,
  output [15:0] r13,
  output [15:0] r6,
  output [15:0] r14,
  output [15:0] r7,
  output [15:0] r15,
  output [15:0] S,
  output [15:0] T
);

  // Register_File__WRITE register_file_write_1: pin names not known; wires that end beside it: Data, clock, Write, rd, Reset, r0, r1, r2, r3, r4, r5, r6, r7, r8, r9, r10, r11, r12, r13, r14, r15
  // Register_File__READ register_file_read_1: pin names not known; wires that end beside it: rs, r0, r1, r2, r3, r4, r5, r6, r7, r8, r9, r10, r11, r12, r13, r14, r15, rt, S, T

  // Notes on the sheet:
  //   WRITE
  //   READ
endmodule

module controlUnit (
  input  [15:0] Instruction,
  output [15:0] Immediate,
  output WriteEnabled,
  output LD__RamBlock,
  output STR__RamBlock,
  output load_store__Mux_s,
  output jal,
  output ori_lui,
  output lui,
  output jr,
  output bne,
  output [3:0] ALU_OPCODE
);

  wire and_2_out, and_4_out;

  Immediate immediate_1 (.Input(Instruction), .out_2(Immediate));
  and and_1 (STR__RamBlock, Instruction[12], Instruction[13], Instruction[14], Instruction[15]);
  and and_2 (and_2_out, Instruction[15], ~Instruction[14], Instruction[13], ~Instruction[12]);  // AND_Gate
  and and_3 (lui, Instruction[15], ~Instruction[14], Instruction[13], Instruction[12]);  // AND_Gate
  and and_4 (and_4_out, Instruction[15], Instruction[14], Instruction[13], ~Instruction[12]);  // AND_Gate
  and and_5 (jal, Instruction[15], ~Instruction[14], ~Instruction[13], Instruction[12]);  // AND_Gate
  and and_6 (bne, Instruction[15], Instruction[14], ~Instruction[13], Instruction[12]);  // AND_Gate
  and and_7 (jr, Instruction[15], Instruction[14], ~Instruction[13], ~Instruction[12]);  // AND_Gate
  not not_1 (WriteEnabled, bne);
  or or_1 (LD__RamBlock, STR__RamBlock, and_4_out);
  or or_2 (load_store__Mux_s, STR__RamBlock, and_4_out);
  or or_3 (ori_lui, and_2_out, lui);

  assign ALU_OPCODE = Instruction[15:12];

  // Notes on the sheet:
  //   OPCODE BIT 3
  //   OPCODE BIT 2
  //   OPCODE BIT 1
  //   OPCODE BIT 0
  //   OPCODE
  //   Detect SW
  //   Detect ORI
  //   Detect LUI
  //   Detect LW
  //   Detect JAL
  //   Detect BNE
  //   Detect JR
  //   1111
  //   1010
  //   1011
  //   1110
  //   1001
  //   1101
  //   1100
endmodule

module Immediate (
  input  [15:0] Input,
  output [15:0] out_2
);

  wire [15:0] bit_extender_1_out, bit_extender_2_out, bit_extender_3_out, bit_extender_4_out,
       bit_extender_5_out;

  assign bit_extender_1_out = {{4{1'b0}}, Input[11:0]};  // Bit_Extender bit_extender_1
  assign bit_extender_2_out = {{8{1'b0}}, Input[7:0]};  // Bit_Extender bit_extender_2
  assign bit_extender_3_out = {{8{Input[7]}}, Input[7:0]};  // Bit_Extender bit_extender_3
  assign bit_extender_4_out = {{12{Input[3]}}, Input[3:0]};  // Bit_Extender bit_extender_4
  assign bit_extender_5_out = {{12{1'b0}}, Input[3:0]};  // Bit_Extender bit_extender_5
  Multiplexer #(.select(4), .width(16)) multiplexer_1 (
    .in0({16{1'b0}}), .in1({16{1'b0}}), .in2({16{1'b0}}), .in3({16{1'b0}}), .in4({16{1'b0}}),
    .in5({16{1'b0}}), .in6({16{1'b0}}), .in7({16{1'b0}}), .in8({16{1'b0}}), .in9(bit_extender_1_out),
    .in10(bit_extender_2_out), .in11(bit_extender_2_out), .in12(bit_extender_3_out),
    .in13(bit_extender_4_out), .in14(bit_extender_5_out), .in15(bit_extender_5_out), .out(out_2),
    .sel(Input[15:12]));  // open: en

  // Notes on the sheet:
  //   JAL
  //   ORI/LUI
  //   JR
  //   BNE
  //   LW/SW
  //   OpCode
endmodule
