// Logisim project project4.circ as structural Verilog: 7 circuits, main circuit 16bit Register
module _16bit_Register (
  input  Write_Enabled,
  input  Reset,
  input  C,
  input  [15:0] D,
  output [15:0] Q
);

  wire not_1_out;

  not not_1 (not_1_out, C);
  D_Flip_Flop d_ff_1 (.clk(not_1_out), .D(D[0]), .Q(Q[0]), .en(Write_Enabled), .reset(Reset));  // open: Qn, preset
  D_Flip_Flop d_ff_2 (.clk(not_1_out), .D(D[1]), .Q(Q[1]), .en(Write_Enabled), .reset(Reset));  // open: Qn, preset
  D_Flip_Flop d_ff_3 (.clk(not_1_out), .D(D[2]), .Q(Q[2]), .en(Write_Enabled), .reset(Reset));  // open: Qn, preset
  D_Flip_Flop d_ff_4 (.clk(not_1_out), .D(D[3]), .Q(Q[3]), .en(Write_Enabled), .reset(Reset));  // open: Qn, preset
  D_Flip_Flop d_ff_5 (.clk(not_1_out), .D(D[4]), .Q(Q[4]), .en(Write_Enabled), .reset(Reset));  // open: Qn, preset
  D_Flip_Flop d_ff_6 (.clk(not_1_out), .D(D[5]), .Q(Q[5]), .en(Write_Enabled), .reset(Reset));  // open: Qn, preset
  D_Flip_Flop d_ff_7 (.clk(not_1_out), .D(D[6]), .Q(Q[6]), .en(Write_Enabled), .reset(Reset));  // open: Qn, preset
  D_Flip_Flop d_ff_8 (.clk(not_1_out), .D(D[7]), .Q(Q[7]), .en(Write_Enabled), .reset(Reset));  // open: Qn, preset
  D_Flip_Flop d_ff_9 (.clk(not_1_out), .D(D[8]), .Q(Q[8]), .en(Write_Enabled), .reset(Reset));  // open: Qn, preset
  D_Flip_Flop d_ff_10 (.clk(not_1_out), .D(D[9]), .Q(Q[9]), .en(Write_Enabled), .reset(Reset));  // open: Qn, preset
  D_Flip_Flop d_ff_11 (.clk(not_1_out), .D(D[10]), .Q(Q[10]), .en(Write_Enabled), .reset(Reset));  // open: Qn, preset
  D_Flip_Flop d_ff_12 (.clk(not_1_out), .D(D[11]), .Q(Q[11]), .en(Write_Enabled), .reset(Reset));  // open: Qn, preset
  D_Flip_Flop d_ff_13 (.clk(not_1_out), .D(D[12]), .Q(Q[12]), .en(Write_Enabled), .reset(Reset));  // open: Qn, preset
  D_Flip_Flop d_ff_14 (.clk(not_1_out), .D(D[13]), .Q(Q[13]), .en(Write_Enabled), .reset(Reset));  // open: Qn, preset
  D_Flip_Flop d_ff_15 (.clk(not_1_out), .D(D[14]), .Q(Q[14]), .en(Write_Enabled), .reset(Reset));  // open: Qn, preset
  D_Flip_Flop d_ff_16 (.clk(not_1_out), .D(D[15]), .Q(Q[15]), .en(Write_Enabled), .reset(Reset));  // open: Qn, preset
endmodule

module Register_File__READ (
  input  [3:0] Read_1,
  input  [15:0] in_2,
  input  [15:0] in_3,
  input  [15:0] in_4,
  input  [15:0] in_5,
  input  [15:0] in_6,
  input  [15:0] in_7,
  input  [15:0] in_8,
  input  [15:0] in_9,
  input  [15:0] in_10,
  input  [15:0] in_11,
  input  [15:0] in_12,
  input  [15:0] in_13,
  input  [15:0] in_14,
  input  [15:0] in_15,
  input  [15:0] in_16,
  input  [15:0] in_17,
  input  [3:0] Read_2,
  output [15:0] Data_1,
  output [15:0] Data_2
);

  Multiplexer #(.select(4), .width(16)) multiplexer_1 (
    .in0(in_2), .in1(in_3), .in2(in_4), .in3(in_5), .in4(in_6), .in5(in_7), .in6(in_8), .in7(in_9),
    .in8(in_10), .in9(in_11), .in10(in_12), .in11(in_13), .in12(in_14), .in13(in_15), .in14(in_16),
    .in15(in_17), .out(Data_1), .sel(Read_1));  // open: en
  Multiplexer #(.select(4), .width(16)) multiplexer_2 (
    .in0(in_2), .in1(in_3), .in2(in_4), .in3(in_5), .in4(in_6), .in5(in_7), .in6(in_8), .in7(in_9),
    .in8(in_10), .in9(in_11), .in10(in_12), .in11(in_13), .in12(in_14), .in13(in_15), .in14(in_16),
    .in15(in_17), .out(Data_2), .sel(Read_2));  // open: en
endmodule

module Register_File__WRITE (
  input  Clockwrite,
  input  Write,
  input  Reset,
  input  [3:0] Selector,
  input  [15:0] Register_Data,
  output [15:0] out_6,
  output [15:0] out_7,
  output [15:0] out_8,
  output [15:0] out_9,
  output [15:0] out_10,
  output [15:0] out_11,
  output [15:0] out_12,
  output [15:0] out_13,
  output [15:0] out_14,
  output [15:0] out_15,
  output [15:0] out_16,
  output [15:0] out_17,
  output [15:0] out_18,
  output [15:0] out_19,
  output [15:0] out_20,
  output [15:0] out_21
);

  wire and_1_out, and_2_out, and_3_out, and_4_out, and_5_out, and_6_out, and_7_out, and_8_out, and_9_out,
       and_10_out, and_11_out, and_12_out, and_13_out, and_14_out, and_15_out, and_16_out, decoder_1_out0,
       decoder_1_out1, decoder_1_out2, decoder_1_out3, decoder_1_out4, decoder_1_out5, decoder_1_out6,
       decoder_1_out7, decoder_1_out8, decoder_1_out9, decoder_1_out10, decoder_1_out11, decoder_1_out12,
       decoder_1_out13, decoder_1_out14, decoder_1_out15;
  wire [15:0] n16bit_register_1_q;

  Decoder #(.select(4)) decoder_1 (
    .out0(decoder_1_out0), .out1(decoder_1_out1), .out2(decoder_1_out2), .out3(decoder_1_out3),
    .out4(decoder_1_out4), .out5(decoder_1_out5), .out6(decoder_1_out6), .out7(decoder_1_out7),
    .out8(decoder_1_out8), .out9(decoder_1_out9), .out10(decoder_1_out10), .out11(decoder_1_out11),
    .out12(decoder_1_out12), .out13(decoder_1_out13), .out14(decoder_1_out14), .out15(decoder_1_out15),
    .sel(Selector));  // open: en
  and and_1 (and_1_out, Clockwrite, decoder_1_out0);
  and and_2 (and_2_out, Clockwrite, decoder_1_out1);
  and and_3 (and_3_out, Clockwrite, decoder_1_out2);
  and and_4 (and_4_out, Clockwrite, decoder_1_out3);
  and and_5 (and_5_out, Clockwrite, decoder_1_out4);
  and and_6 (and_6_out, Clockwrite, decoder_1_out5);
  and and_7 (and_7_out, Clockwrite, decoder_1_out6);
  and and_8 (and_8_out, Clockwrite, decoder_1_out7);
  and and_9 (and_9_out, Clockwrite, decoder_1_out8);
  and and_10 (and_10_out, Clockwrite, decoder_1_out9);
  and and_11 (and_11_out, Clockwrite, decoder_1_out10);
  and and_12 (and_12_out, Clockwrite, decoder_1_out11);
  and and_13 (and_13_out, Clockwrite, decoder_1_out12);
  and and_14 (and_14_out, Clockwrite, decoder_1_out13);
  and and_15 (and_15_out, Clockwrite, decoder_1_out14);
  and and_16 (and_16_out, Clockwrite, decoder_1_out15);
  _16bit_Register u_16bit_register_1 (
    .C(and_1_out), .D(Register_Data), .Write_Enabled(Write), .Reset(Reset), .Q(n16bit_register_1_q));
  _16bit_Register u_16bit_register_2 (
    .C(and_2_out), .D(Register_Data), .Write_Enabled(Write), .Reset(Reset), .Q(out_7));
  _16bit_Register u_16bit_register_3 (
    .C(and_3_out), .D(Register_Data), .Write_Enabled(Write), .Reset(Reset), .Q(out_8));
  _16bit_Register u_16bit_register_4 (
    .C(and_4_out), .D(Register_Data), .Write_Enabled(Write), .Reset(Reset), .Q(out_9));
  _16bit_Register u_16bit_register_5 (
    .C(and_5_out), .D(Register_Data), .Write_Enabled(Write), .Reset(Reset), .Q(out_10));
  _16bit_Register u_16bit_register_6 (
    .C(and_6_out), .D(Register_Data), .Write_Enabled(Write), .Reset(Reset), .Q(out_11));
  _16bit_Register u_16bit_register_7 (
    .C(and_7_out), .D(Register_Data), .Write_Enabled(Write), .Reset(Reset), .Q(out_12));
  _16bit_Register u_16bit_register_8 (
    .C(and_8_out), .D(Register_Data), .Write_Enabled(Write), .Reset(Reset), .Q(out_13));
  _16bit_Register u_16bit_register_9 (
    .C(and_9_out), .D(Register_Data), .Write_Enabled(Write), .Reset(Reset), .Q(out_14));
  _16bit_Register u_16bit_register_10 (
    .C(and_10_out), .D(Register_Data), .Write_Enabled(Write), .Reset(Reset), .Q(out_15));
  _16bit_Register u_16bit_register_11 (
    .C(and_11_out), .D(Register_Data), .Write_Enabled(Write), .Reset(Reset), .Q(out_16));
  _16bit_Register u_16bit_register_12 (
    .C(and_12_out), .D(Register_Data), .Write_Enabled(Write), .Reset(Reset), .Q(out_17));
  _16bit_Register u_16bit_register_13 (
    .C(and_13_out), .D(Register_Data), .Write_Enabled(Write), .Reset(Reset), .Q(out_18));
  _16bit_Register u_16bit_register_14 (
    .C(and_14_out), .D(Register_Data), .Write_Enabled(Write), .Reset(Reset), .Q(out_19));
  _16bit_Register u_16bit_register_15 (
    .C(and_15_out), .D(Register_Data), .Write_Enabled(Write), .Reset(Reset), .Q(out_20));
  _16bit_Register u_16bit_register_16 (
    .C(and_16_out), .D(Register_Data), .Write_Enabled(Write), .Reset(Reset), .Q(out_21));

  assign out_6 = {16{1'b0}};

  // Notes on the sheet:
  //   16Bit Registers
endmodule

module Register_File (
  input  Reset,
  input  Write,
  input  [3:0] rs,
  input  [15:0] Data,
  input  [3:0] rd,
  input  [3:0] rt,
  output [15:0] S,
  output [15:0] T
);

  wire Clock_out;
  wire [15:0] register_file_write_1_out_6, register_file_write_1_out_7, register_file_write_1_out_8,
       register_file_write_1_out_9, register_file_write_1_out_10, register_file_write_1_out_11,
       register_file_write_1_out_12, register_file_write_1_out_13, register_file_write_1_out_14,
       register_file_write_1_out_15, register_file_write_1_out_16, register_file_write_1_out_17,
       register_file_write_1_out_18, register_file_write_1_out_19, register_file_write_1_out_20,
       register_file_write_1_out_21;

  Clock Clock (.out(Clock_out));
  Register_File__WRITE register_file_write_1 (
    .Register_Data(Data), .Clockwrite(Clock_out), .Write(Write), .Reset(Reset), .Selector(rd),
    .out_6(register_file_write_1_out_6), .out_7(register_file_write_1_out_7),
    .out_8(register_file_write_1_out_8), .out_9(register_file_write_1_out_9),
    .out_10(register_file_write_1_out_10), .out_11(register_file_write_1_out_11),
    .out_12(register_file_write_1_out_12), .out_13(register_file_write_1_out_13),
    .out_14(register_file_write_1_out_14), .out_15(register_file_write_1_out_15),
    .out_16(register_file_write_1_out_16), .out_17(register_file_write_1_out_17),
    .out_18(register_file_write_1_out_18), .out_19(register_file_write_1_out_19),
    .out_20(register_file_write_1_out_20), .out_21(register_file_write_1_out_21));
  Register_File__READ register_file_read_1 (
    .Read_1(rs), .in_2(register_file_write_1_out_6), .in_3(register_file_write_1_out_7),
    .in_4(register_file_write_1_out_8), .in_5(register_file_write_1_out_9),
    .in_6(register_file_write_1_out_10), .in_7(register_file_write_1_out_11),
    .in_8(register_file_write_1_out_12), .in_9(register_file_write_1_out_13),
    .in_10(register_file_write_1_out_14), .in_11(register_file_write_1_out_15),
    .in_12(register_file_write_1_out_16), .in_13(register_file_write_1_out_17),
    .in_14(register_file_write_1_out_18), .in_15(register_file_write_1_out_19),
    .in_16(register_file_write_1_out_20), .in_17(register_file_write_1_out_21), .Read_2(rt), .Data_1(S),
    .Data_2(T));

  // Notes on the sheet:
  //   WRITE
  //   READ
endmodule

module Counter (
  input  Clock,
  input  [15:0] D,
  output [15:0] Output
);

  wire comparator_1_eq;
  wire [15:0] _16Bit_Adder_output;

  _16_Bit_Adder__CLA _16Bit_Adder (
    .A({16{1'b0}}), .B(Output), .CarryIn(Clock), .Output(_16Bit_Adder_output));  // open: CarryOut
  Comparator #(.width(16)) comparator_1 (.a(Output), .b(D), .eq(comparator_1_eq));  // open: gt, lt
  _16bit_Register _16Bit_Register (
    .C(Clock), .D(_16Bit_Adder_output), .Write_Enabled(1'b1), .Reset(comparator_1_eq), .Q(Output));

  // Notes on the sheet:
  //   MaxValue
  //   Write Enabled
  //   reset
endmodule

module Clock_Divider (
  input  Clock,
  input  [15:0] D,
  output Divided
);

  wire comparator_1_eq, d_ff_1_qn;
  wire [15:0] _16Bit_Adder_output, _16Bit_Register_q, shifter_1_out;

  Shifter #(.width(16), .shift("lr")) shifter_1 (.in(D), .\dist (4'b0001), .out(shifter_1_out));
  _16_Bit_Adder__CLA _16Bit_Adder (
    .A({16{1'b0}}), .B(_16Bit_Register_q), .CarryIn(Clock), .Output(_16Bit_Adder_output));  // open: CarryOut
  Comparator #(.width(16)) comparator_1 (
    .a(_16Bit_Register_q), .b(shifter_1_out), .eq(comparator_1_eq));  // open: gt, lt
  _16bit_Register _16Bit_Register (
    .C(Clock), .D(_16Bit_Adder_output), .Write_Enabled(1'b1), .Reset(comparator_1_eq), .Q(_16Bit_Register_q));
  D_Flip_Flop d_ff_1 (.clk(comparator_1_eq), .D(d_ff_1_qn), .Q(Divided), .Qn(d_ff_1_qn));  // open: preset, en, reset

  // Notes on the sheet:
  //   MaxValue
  //   Write Enabled
  //   reset
endmodule

module trafic_light (
);

  wire clock_1_out, clock_divider_1_divided, decoder_1_out0, decoder_1_out1, decoder_1_out2, decoder_1_out3,
       decoder_1_out4, decoder_1_out5, decoder_1_out6, decoder_1_out7, decoder_1_out8, decoder_1_out9,
       decoder_1_out10, decoder_1_out11, decoder_1_out12, decoder_1_out13, multiplexer_1_out,
       multiplexer_2_out, multiplexer_3_out, multiplexer_4_out, multiplexer_5_out, multiplexer_6_out,
       or_1_out, or_2_out, or_3_out;
  wire [15:0] counter_1_output;

  Clock clock_1 (.out(clock_1_out));
  Counter counter_1 (.Clock(clock_1_out), .D(16'he), .Output(counter_1_output));
  Clock_Divider clock_divider_1 (.Clock(clock_1_out), .D(16'h1c), .Divided(clock_divider_1_divided));
  Decoder #(.select(4)) decoder_1 (
    .out0(decoder_1_out0), .out1(decoder_1_out1), .out2(decoder_1_out2), .out3(decoder_1_out3),
    .out4(decoder_1_out4), .out5(decoder_1_out5), .out6(decoder_1_out6), .out7(decoder_1_out7),
    .out8(decoder_1_out8), .out9(decoder_1_out9), .out10(decoder_1_out10), .out11(decoder_1_out11),
    .out12(decoder_1_out12), .out13(decoder_1_out13), .sel(counter_1_output[3:0]));  // open: out14, out15, en
  or or_1 (or_1_out, decoder_1_out8, decoder_1_out9, decoder_1_out10, decoder_1_out11);
  or or_2 (or_2_out, decoder_1_out12, decoder_1_out13);
  or or_3 (or_3_out, decoder_1_out0, decoder_1_out1, decoder_1_out2, decoder_1_out3, decoder_1_out4, decoder_1_out5, decoder_1_out6, decoder_1_out7);
  LED led_1 (.in(multiplexer_1_out));
  Multiplexer multiplexer_1 (
    .in0(or_2_out), .in1(1'b1), .out(multiplexer_1_out), .sel(clock_divider_1_divided));  // open: en
  Multiplexer multiplexer_2 (
    .in0(or_1_out), .in1(1'b0), .out(multiplexer_2_out), .sel(clock_divider_1_divided));  // open: en
  LED led_2 (.in(multiplexer_2_out));
  Multiplexer multiplexer_3 (
    .in0(or_3_out), .in1(1'b0), .out(multiplexer_3_out), .sel(clock_divider_1_divided));  // open: en
  LED led_3 (.in(multiplexer_3_out));
  LED led_4 (.in(multiplexer_4_out));
  Multiplexer multiplexer_4 (
    .in0(1'b1), .in1(or_2_out), .out(multiplexer_4_out), .sel(clock_divider_1_divided));  // open: en
  Multiplexer multiplexer_5 (
    .in0(1'b0), .in1(or_1_out), .out(multiplexer_5_out), .sel(clock_divider_1_divided));  // open: en
  LED led_5 (.in(multiplexer_5_out));
  LED led_6 (.in(multiplexer_6_out));
  Multiplexer multiplexer_6 (
    .in0(1'b0), .in1(or_3_out), .out(multiplexer_6_out), .sel(clock_divider_1_divided));  // open: en
endmodule
